# Fritzing sketch Untitled Sketch (saved by Fritzing 1.0.5)
circuit board: 8.46667cm x 5.64444cm
breadboards: 1

parts:
  R1 = Resistor [tolerance=±5% power=0.25W resistance=10k package=THT]
  e_paper = E-Paper Eval Board  # not connected
  ESP32-c3 = Esp32-c3 super mini
  oled = Grove OLED 128x96
  Buzzer = MH-FMD buzzer
  PN532 = PN532 Elechouse RFID NFC Module V3
  元件1 = Adafruit BQ24074 Solar-DC-USB Lipo Charger
  U1 = LIPO-110mAh [package=lipo-110]
  solar_panel = SOLAR-IXYS [package=solarbit-12x1]
  R2 = Photocell (LDR) [power=0.25W dark_resistance_@0.01lx=300kΩ light_resistance_@100lx=400Ω luminance=10lx package=THT]

nets:
  N1: R1.Pin_0, ESP32-c3.Pin_9, R2.pin_1
  GND: R1.Pin_1, ESP32-c3.Pin_14, ESP32-c3.Pin_15, oled.GND, Buzzer.Pin_3, PN532.GND, 元件1.GND, U1.-, solar_panel.A
  N2: ESP32-c3.Pin_1, Buzzer.Pin_2
  N3: ESP32-c3.Pin_4, oled.SDA, PN532.SDA
  N4: ESP32-c3.Pin_5, oled.SCL, PN532.SCL
  N5: ESP32-c3.Pin_16, 元件1.OUT
  VCC: oled.VCC, Buzzer.Pin_1, PN532.VCC, R2.pin_0
  N6: 元件1.VLIPO, U1.+
  N7: 元件1.VBUS, solar_panel.C

custom parts:
  Esp32-c3 super mini: ESP32-C3 Development Board ESP32 SuperMini Development Board ESP32 Development Board WiFi Bluetooth.
  MH-FMD buzzer: MH-FMD buzzer.
  PN532 Elechouse RFID NFC Module V3: NFC is a popular technology in recent years. We often heard this work while smart phone company such as Samsung or HTC introduces their latest high-end phones. Almost all the high-end phone in the market support NFC. Near field communication (NFC) is a set of standards for smart phones and similar devices to establish radio communication with each other by touching them together or bringing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
