# Fritzing sketch bookmark (saved by Fritzing 1.0.5)
circuit board: 8.46667cm x 5.64444cm
breadboards: 1

parts:
  ESP32-c5 = Esp32-c3 super mini
  MP1584_module1 = Mini-360 DC-DC Buck converter [package=THT]
  TP4056_Charger_board1 = TP4056 [chip_label=TP4056 package="DIP (Dual Inline) [THT]"]
  U3 = LIPO-110mAh [package=lipo-110]
  solar_panel2 = SOLAR-IXYS [package=solarbit-12x1]
  R3 = Resistor [tolerance=±5% power=0.25W resistance=10k package=THT]
  R4 = Photocell (LDR) [power=0.25W dark_resistance_@0.01lx=300kΩ light_resistance_@100lx=400Ω luminance=10lx package=THT]
  J1 = Piezo Speaker

nets:
  N1: ESP32-c5.Pin_1, J1.pin2
  N2: ESP32-c5.Pin_9, R3.Pin_0
  N3: ESP32-c5.Pin_14, R4.pin_0
  N4: ESP32-c5.Pin_15, MP1584_module1.OUT-, R3.Pin_1, R4.pin_1, J1.pin1
  N5: ESP32-c5.Pin_16, MP1584_module1.OUT+
  N6: MP1584_module1.IN-, TP4056_Charger_board1.pin5
  N7: MP1584_module1.IN+, TP4056_Charger_board1.pin4
  N8: TP4056_Charger_board1.pin1, solar_panel2.C
  N9: TP4056_Charger_board1.pin2, solar_panel2.A
  N10: TP4056_Charger_board1.pin3, U3.+
  N11: TP4056_Charger_board1.pin6, U3.-

custom parts:
  Esp32-c3 super mini: ESP32-C3 Development Board ESP32 SuperMini Development Board ESP32 Development Board WiFi Bluetooth.
  Mini-360 DC-DC Buck converter: Mini-360 DC-DC Buck converter. Tiny buck step down voltage converter, input voltage 4.75 to 23V output 1 to 17V adjustable. Available from ebay and the like.
  TP4056: A DIP stand-in part for whatever IC you want. With 6 pins on a 300mil dual inline package (DIP) footprint.
